# Fritzing sketch MAU106_+-5V_PSU_PTC (saved by Fritzing 0.9.3b)
breadboards: 2

parts:
  U1 = mystery part, 4 pins [chip_label=NJM2396]
  D1 = Rectifier Diode [part_number=1N4001 package="300 mil [THT]"]
  C1 = Film/Foil Capacitor [capacitance=100nF voltage=35V package="5mm [THT, pp]"]
  C2 = Ceramic Capacitor [capacitance=100nF package="100 mil [THT, multilayer]"]
  C3 = Electrolytic Capacitor [capacitance=1µF package="100 mil [THT, electrolytic]"]
  Power_plug1 = Power plug
  U2 = mystery part, 6 pins [chip_label=MAU106]
  C5 = Electrolytic Capacitor [capacitance=1µF package="100 mil [THT, electrolytic]"]
  R5 = Resistor [tolerance=±5% resistance=680 package=THT]
  R6 = Resistor [tolerance=±5% resistance=1k package=THT]
  C7 = Electrolytic Capacitor [capacitance=1µF package="100 mil [THT, electrolytic]"]
  U3 = mystery part, 12 pins [chip_label="Common Mode"]
  R7 = Resistor [tolerance=±5% resistance=1k package=THT]
  LED1 = LED - 3mm [color="Green (570nm)" package="3 mm [THT]"]
  R8 = Resistor [tolerance=±5% resistance=100k package=THT]
  R9 = Resistor [tolerance=±5% resistance=100k package=THT]
  LED2 = LED - 3mm [color="Red (633nm)" package="3 mm [THT]"]
  LED3 = LED - 3mm [color="Blue (525nm)" package="3 mm [THT]"]
  R10 = Resistor [tolerance=±5% resistance=100 package=THT]
  R11 = Resistor [tolerance=±5% resistance=100 package=THT]
  R12 = Resistor [tolerance=±5% resistance=47 package=THT]
  R13 = Resistor [tolerance=±5% resistance=47 package=THT]
  U4 = mystery part, 2 pins [chip_label=PTC]

nets:
  N1: U1.pin1, U1.pin4, D1.cathode, C1.+, U3.pin1
  N2: U1.pin2, D1.anode, C2.0
  N3: U1.pin3, C1.-, C2.1, U3.pin6
  N4: C3.-, U2.pin2, U2.pin5, C5.+, C7.-, LED1.cathode, R9.Pin_0, LED2.cathode, LED3.anode, R10.Pin_1, R11.Pin_1, R12.Pin_0, R13.Pin_0
  N5: C3.+, R7.Pin_0, R8.Pin_0, R13.Pin_1, U4.pin1
  N6: Power_plug1.GND, U3.pin7
  N7: Power_plug1.VCC, U3.pin12
  N8: U2.pin1, U4.pin2
  N9: U2.pin4, C5.-, R5.Pin_0, R11.Pin_0
  N10: U2.pin6, R6.Pin_0, C7.+, R10.Pin_0
  N11: R5.Pin_1, LED3.cathode
  N12: R6.Pin_1, LED2.anode
  N13: R7.Pin_1, LED1.anode
  N14: R8.Pin_1, R9.Pin_1

notes:
  GND
  6V
  IN(+6V)
  MAU106
  1 +Vin
  2 -Vin
  3 NC
  4 -Vout
  5 Common
  6 +Vout
  GND
  Digital +5V
  Analog -5V
  Analog +5V
  Power
  Monitor(2.5V)
