# Fritzing sketch MAU106_EMI_Test (saved by Fritzing 0.9.3b)
breadboards: 1

parts:
  U1 = mystery part, 6 pins [chip_label=MAU106]
  C1 = Electrolytic Capacitor [capacitance=1µF package="100 mil [THT, electrolytic]"]
  C2 = Electrolytic Capacitor [capacitance=1µF package="100 mil [THT, electrolytic]"]
  C3 = Electrolytic Capacitor [capacitance=1µF package="100 mil [THT, electrolytic]"]
  R1 = Resistor [tolerance=±5% resistance=1k package=THT]
  R2 = Resistor [tolerance=±5% resistance=1k package=THT]
  U2 = mystery part, 3 pins [chip_label=EMIFIL]
  U3 = mystery part, 3 pins [chip_label=EMIFIL]
  R3 = Resistor [tolerance=±5% resistance=100 package=THT]
  R4 = Resistor [tolerance=±5% resistance=100 package=THT]

nets:
  N1: U1.pin1, C3.+
  N2: U1.pin2, U1.pin5, C1.-, C2.+, C3.-, R1.Pin_1, R2.Pin_1, U2.pin2, U3.pin2, R3.Pin_1, R4.Pin_1
  N3: U1.pin4, C2.-, R2.Pin_0, U3.pin1
  N4: U1.pin6, C1.+, R1.Pin_0, U2.pin1
  N5: U2.pin3, R3.Pin_0
  N6: U3.pin3, R4.Pin_0

notes:
  MAU106
  1 +Vin
  2 -Vin
  3 NC
  4 -Vout
  5 Common
  6 +Vout
  GND
  +Vin
  -Vout
  +Vout
  +Vout
  -Vout
