# Fritzing sketch MAU106_LC_LPF_Test (saved by Fritzing 0.9.3b)
breadboards: 1

parts:
  U1 = mystery part, 6 pins [chip_label=MAU106]
  C2 = Electrolytic Capacitor [capacitance=1µF package="100 mil [THT, electrolytic]"]
  C3 = Electrolytic Capacitor [capacitance=1µF package="100 mil [THT, electrolytic]"]
  R1 = Resistor [tolerance=±5% resistance=1k package=THT]
  R2 = Resistor [tolerance=±5% resistance=1k package=THT]
  R3 = Resistor [tolerance=±5% resistance=100 package=THT]
  R4 = Resistor [tolerance=±5% resistance=100 package=THT]
  C4 = Electrolytic Capacitor [capacitance=1µF package="100 mil [THT, electrolytic]"]
  L1 = Inductor [package="400 mil [THT]"]
  L2 = Inductor [package="400 mil [THT]"]

nets:
  N1: U1.pin1, C3.+
  N2: U1.pin2, U1.pin5, C2.+, C3.-, R1.Pin_1, R2.Pin_1, R3.Pin_1, R4.Pin_1, C4.-
  N3: U1.pin4, L1.pin_1
  N4: U1.pin6, L2.pin_1
  N5: C2.-, R2.Pin_0, R4.Pin_0, L1.pin_0
  N6: R1.Pin_0, R3.Pin_0, C4.+, L2.pin_0

notes:
  MAU106
  1 +Vin
  2 -Vin
  3 NC
  4 -Vout
  5 Common
  6 +Vout
  GND
  +Vin
  -Vout
  +Vout
