# Fritzing sketch NJM2396+MAU106_Output_ComonModeChoke (saved by Fritzing 0.9.3b)
breadboards: 2

parts:
  U1 = mystery part, 4 pins [chip_label=NJM2396]
  D1 = Rectifier Diode [part_number=1N4001 package="300 mil [THT]"]
  C1 = Film/Foil Capacitor [capacitance=100nF voltage=35V package="5mm [THT, pp]"]
  C2 = Ceramic Capacitor [capacitance=100nF package="100 mil [THT, multilayer]"]
  C3 = Electrolytic Capacitor [capacitance=1µF package="100 mil [THT, electrolytic]"]
  R1 = Resistor [tolerance=±5% resistance=47 package=THT]
  R2 = Resistor [tolerance=±5% resistance=47 package=THT]
  Power_plug1 = Power plug
  U2 = mystery part, 6 pins [chip_label=MAU106]
  C5 = Electrolytic Capacitor [capacitance=1µF package="100 mil [THT, electrolytic]"]
  R5 = Resistor [tolerance=±5% resistance=1k package=THT]
  R6 = Resistor [tolerance=±5% resistance=1k package=THT]
  R7 = Resistor [tolerance=±5% resistance=100 package=THT]
  R8 = Resistor [tolerance=±5% resistance=100 package=THT]
  C7 = Electrolytic Capacitor [capacitance=1µF package="100 mil [THT, electrolytic]"]
  U3 = mystery part, 12 pins [chip_label="Common Mode"]
  U4 = mystery part, 12 pins [chip_label="Common Mode"]

nets:
  N1: U1.pin1, U1.pin4, D1.cathode, C1.+, U3.pin1
  N2: U1.pin2, D1.anode, C2.0, R1.Pin_0
  N3: U1.pin3, C1.-, C2.1, R1.Pin_1, U3.pin6
  N4: C3.-, R2.Pin_1, U2.pin2, U2.pin5, C5.+, R5.Pin_1, R6.Pin_1, R7.Pin_1, R8.Pin_1, C7.-
  N5: C3.+, R2.Pin_0, U2.pin1
  N6: Power_plug1.GND, U3.pin7
  N7: Power_plug1.VCC, U3.pin12
  N8: U2.pin4, R6.Pin_0, U4.pin1
  N9: U2.pin6, R5.Pin_0, U4.pin6
  N10: C5.-, R7.Pin_0, U4.pin12
  N11: R8.Pin_0, C7.+, U4.pin7

notes:
  GND
  6V
  IN(+6V)
  MAU106
  1 +Vin
  2 -Vin
  3 NC
  4 -Vout
  5 Common
  6 +Vout
  GND
  Digital +5V
  Analog -5V
  Analog +5V
