# Fritzing sketch NJM2396_Test (saved by Fritzing 0.9.3b)
breadboards: 1

parts:
  U1 = mystery part, 4 pins [chip_label=NJM2396]
  D1 = Rectifier Diode [part_number=1N4001 package="300 mil [THT]"]
  C1 = Film/Foil Capacitor [capacitance=100nF voltage=35V package="5mm [THT, pp]"]
  C2 = Ceramic Capacitor [capacitance=100nF package="100 mil [THT, multilayer]"]
  C3 = Electrolytic Capacitor [capacitance=1µF package="100 mil [THT, electrolytic]"]
  R1 = Resistor [tolerance=±5% resistance=47 package=THT]
  R2 = Resistor [tolerance=±5% resistance=47 package=THT]
  R3 = Resistor [tolerance=±5% resistance=47 package=THT]
  L1 = Inductor [package="400 mil [THT]"]
  C4 = Electrolytic Capacitor [capacitance=1µF package="100 mil [THT, electrolytic]"]
  Power_plug1 = Power plug

nets:
  N1: U1.pin1, U1.pin4, D1.cathode, C1.+, L1.pin_1, C4.+
  N2: U1.pin2, D1.anode, C2.0, C3.+, R1.Pin_1, R2.Pin_1, R3.Pin_1
  N3: U1.pin3, C1.-, C2.1, C3.-, R1.Pin_0, R2.Pin_0, R3.Pin_0, C4.-, Power_plug1.GND
  N4: L1.pin_0, Power_plug1.VCC

notes:
  GND
  OUT(5V)
  GND
  6V
  IN(6V)
